# Fritzing sketch Power supply (saved by Fritzing 0.9.10b)

parts:
  AMS4 = AMS1777 5V regulator module
  AMS5 = AMS1777 5V regulator module
  AMS6 = AMS1777 5V regulator module
  TP3 = TP4056 [chip_label=TP4056 package="DIP (Dual Inline) [THT]"]
  TP4 = TP4056 [chip_label=TP4056 package="DIP (Dual Inline) [THT]"]
  Digital_Panel_Meter_Voltage_DMS-20PC_by_Murata2 = Digital Panel Meter, Voltage, DMS-20PC
  ON/OFF2 = SWITCH-MOMENTARY-2 [package=reed_switch_plastic]
  S5 = TILT-SWITCH-SW-200D [package=reed_switch_plastic]
  S6 = TILT-SWITCH-SW-200D [package=reed_switch_plastic]
  D5 = SOLAR-IXYS [package=solarbit-12x1]
  D6 = SOLAR-IXYS [package=solarbit-12x1]
  5_VDC_Connector1 = Power Jack [package=power_jack_pth_lock]
  3_7_VCC3 = Battery Holders [package=battery-aa]
  3_7_VCC4 = Battery Holders [package=battery-aa]

nets:
  N1: AMS4.VIN+, TP3.pin3, TP4.pin3
  N2: AMS4.GND-_(input), TP3.pin6, TP4.pin6
  N3: AMS4.VOUT+, ON/OFF2.1
  N4: AMS4.GND-_(output), Digital_Panel_Meter_Voltage_DMS-20PC_by_Murata2.3:_GND, 5_VDC_Connector1.GND
  N5: AMS5.VIN+, S5.2
  N6: AMS5.GND-_(input), D5.A
  N7: AMS5.VOUT+, TP3.pin1
  N8: AMS5.GND-_(output), TP3.pin2
  N9: AMS6.VIN+, S6.2
  N10: AMS6.GND-_(input), D6.A
  N11: AMS6.VOUT+, TP4.pin1
  N12: AMS6.GND-_(output), TP4.pin2
  N13: TP3.pin4, 3_7_VCC4.+
  N14: TP3.pin5, 3_7_VCC4.-
  N15: TP4.pin4, 3_7_VCC3.+
  N16: TP4.pin5, 3_7_VCC3.-
  N17: Digital_Panel_Meter_Voltage_DMS-20PC_by_Murata2.1:_VCC, ON/OFF2.2, 5_VDC_Connector1.PWR
  N18: S5.1, D5.C
  N19: S6.1, D6.C

custom parts:
  AMS1777 5V regulator module: AMS1777 5V regulator module source : https://github.com/ShenTengTu/fritzing_parts/tree/master/voltage%20regulator/AMS1117_5V_regulator_module
  TP4056: A DIP stand-in part for whatever IC you want. With 6 pins on a 300mil dual inline package (DIP) footprint.
